// Logisim project project1.circ as structural Verilog
module nandgate (
  input  b,
  input  a,
  output out_3
);

  wire pull_resistor_1_node, transistor_2_out;

  Pull_Resistor pull_resistor_1 (.node(pull_resistor_1_node));
  Pull_Resistor pull_resistor_2 (.node(a));
  Transistor transistor_1 (.in(pull_resistor_1_node), .out(out_3), .gate(a));
  Pull_Resistor pull_resistor_3 (.node(b));
  Pull_Resistor pull_resistor_4 (.node(out_3));
  Transistor transistor_2 (.in(out_3), .out(transistor_2_out), .gate(b));
  // also tied to GND on the sheet: transistor_2_out
  // also tied to VCC on the sheet: pull_resistor_1_node
endmodule

module notgate (
  input  in_1,
  output out_2
);

  nand nand_1 (out_2, in_1, in_1);
endmodule

module andgate (
  input  a,
  input  b,
  output o
);

  wire nand_1_out;

  nand nand_1 (nand_1_out, a, b);
  // Probe on nand_1_out
  notgate notgate_1 (.in_1(nand_1_out), .out_2(o));
endmodule

module orgate (
  input  a,
  input  b,
  output o
);

  wire notgate_1_out_2, notgate_2_out_2;

  notgate notgate_1 (.in_1(a), .out_2(notgate_1_out_2));
  notgate notgate_2 (.in_1(b), .out_2(notgate_2_out_2));
  nand nand_1 (o, notgate_1_out_2, notgate_2_out_2);
endmodule

module not16 (
  input  [15:0] x,
  output [15:0] o
);

  notgate notgate_1 (.in_1(x[0]), .out_2(o[0]));
  notgate notgate_2 (.in_1(x[1]), .out_2(o[1]));
  notgate notgate_3 (.in_1(x[2]), .out_2(o[2]));
  notgate notgate_4 (.in_1(x[3]), .out_2(o[3]));
  notgate notgate_5 (.in_1(x[4]), .out_2(o[4]));
  notgate notgate_6 (.in_1(x[5]), .out_2(o[5]));
  notgate notgate_7 (.in_1(x[6]), .out_2(o[6]));
  notgate notgate_8 (.in_1(x[7]), .out_2(o[7]));
  notgate notgate_9 (.in_1(x[8]), .out_2(o[8]));
  notgate notgate_10 (.in_1(x[9]), .out_2(o[9]));
  notgate notgate_11 (.in_1(x[10]), .out_2(o[10]));
  notgate notgate_12 (.in_1(x[11]), .out_2(o[11]));
  notgate notgate_13 (.in_1(x[12]), .out_2(o[12]));
  notgate notgate_14 (.in_1(x[13]), .out_2(o[13]));
  notgate notgate_15 (.in_1(x[14]), .out_2(o[14]));
  notgate notgate_16 (.in_1(x[15]), .out_2(o[15]));
endmodule

module and16 (
  input  [15:0] a,
  input  [15:0] b,
  output [15:0] o
);

  andgate andgate_1 (.a(a[0]), .b(b[0]), .o(o[0]));
  andgate andgate_2 (.a(a[1]), .b(b[1]), .o(o[1]));
  andgate andgate_3 (.a(a[2]), .b(b[2]), .o(o[2]));
  andgate andgate_4 (.a(a[3]), .b(b[3]), .o(o[3]));
  andgate andgate_5 (.a(a[4]), .b(b[4]), .o(o[4]));
  andgate andgate_6 (.a(a[5]), .b(b[5]), .o(o[5]));
  andgate andgate_7 (.a(a[6]), .b(b[6]), .o(o[6]));
  andgate andgate_8 (.a(a[7]), .b(b[7]), .o(o[7]));
  andgate andgate_9 (.a(a[8]), .b(b[8]), .o(o[8]));
  andgate andgate_10 (.a(a[9]), .b(b[9]), .o(o[9]));
  andgate andgate_11 (.a(a[10]), .b(b[10]), .o(o[10]));
  andgate andgate_12 (.a(a[11]), .b(b[11]), .o(o[11]));
  andgate andgate_13 (.a(a[12]), .b(b[12]), .o(o[12]));
  andgate andgate_14 (.a(a[13]), .b(b[13]), .o(o[13]));
  andgate andgate_15 (.a(a[14]), .b(b[14]), .o(o[14]));
  andgate andgate_16 (.a(a[15]), .b(b[15]), .o(o[15]));
endmodule

module or16 (
  input  [15:0] a,
  input  [15:0] b,
  output [15:0] o
);

  wire [15:0] and16_1_o, not16_1_o, not16_2_o;

  not16 not16_1 (.x(a), .o(not16_1_o));
  not16 not16_2 (.x(b), .o(not16_2_o));
  // Probe on not16_1_o
  // Probe on not16_2_o
  and16 and16_1 (.a(not16_1_o), .b(not16_2_o), .o(and16_1_o));
  // Probe on and16_1_o
  not16 not16_3 (.x(and16_1_o), .o(o));
endmodule

module xorgate (
  input  a,
  input  b,
  output o
);

  wire andgate_1_o, andgate_2_o, notgate_1_out_2, notgate_2_out_2;

  notgate notgate_1 (.in_1(a), .out_2(notgate_1_out_2));
  notgate notgate_2 (.in_1(b), .out_2(notgate_2_out_2));
  andgate andgate_1 (.a(a), .b(notgate_2_out_2), .o(andgate_1_o));
  andgate andgate_2 (.a(notgate_1_out_2), .b(b), .o(andgate_2_o));
  orgate orgate_1 (.a(andgate_1_o), .b(andgate_2_o), .o(o));
endmodule

module or8way (
  input  [7:0] a,
  output o
);

  wire orgate_1_o, orgate_2_o, orgate_3_o, orgate_4_o, orgate_5_o, orgate_6_o;

  orgate orgate_1 (.a(a[0]), .b(a[1]), .o(orgate_1_o));
  orgate orgate_2 (.a(orgate_1_o), .b(a[2]), .o(orgate_2_o));
  orgate orgate_3 (.a(orgate_2_o), .b(a[3]), .o(orgate_3_o));
  orgate orgate_4 (.a(a[4]), .b(a[5]), .o(orgate_4_o));
  orgate orgate_5 (.a(a[6]), .b(a[7]), .o(orgate_5_o));
  orgate orgate_6 (.a(orgate_3_o), .b(orgate_4_o), .o(orgate_6_o));
  orgate orgate_7 (.a(orgate_5_o), .b(orgate_6_o), .o(o));
endmodule

module mux (
  input  a,
  input  b,
  input  sel,
  output o
);

  wire andgate_1_o, andgate_2_o, notgate_1_out_2, orgate_1_o;

  orgate orgate_1 (.a(b), .b(notgate_1_out_2), .o(orgate_1_o));
  andgate andgate_1 (.a(orgate_1_o), .b(a), .o(andgate_1_o));
  notgate notgate_1 (.in_1(sel), .out_2(notgate_1_out_2));
  andgate andgate_2 (.a(b), .b(sel), .o(andgate_2_o));
  orgate orgate_2 (.a(andgate_2_o), .b(andgate_1_o), .o(o));
endmodule

module Dmux (
  input  x,
  input  sel,
  output a,
  output b
);

  wire notgate_1_out_2;

  notgate notgate_1 (.in_1(sel), .out_2(notgate_1_out_2));
  andgate andgate_1 (.a(x), .b(notgate_1_out_2), .o(a));
  andgate andgate_2 (.a(x), .b(sel), .o(b));
endmodule

module mux16 (
  input  sel,
  input  [15:0] a,
  input  [15:0] b,
  output [15:0] o
);

  mux mux_1 (.a(a[0]), .b(b[0]), .sel(sel), .o(o[0]));
  mux mux_2 (.a(a[1]), .b(b[1]), .sel(sel), .o(o[1]));
  mux mux_3 (.a(a[2]), .b(b[2]), .sel(sel), .o(o[2]));
  mux mux_4 (.a(a[3]), .b(b[3]), .sel(sel), .o(o[3]));
  mux mux_5 (.a(a[4]), .b(b[4]), .sel(sel), .o(o[4]));
  mux mux_6 (.a(a[5]), .b(b[5]), .sel(sel), .o(o[5]));
  mux mux_7 (.a(a[6]), .b(b[6]), .sel(sel), .o(o[6]));
  mux mux_8 (.a(a[7]), .b(b[7]), .sel(sel), .o(o[7]));
  mux mux_9 (.a(a[8]), .b(b[8]), .sel(sel), .o(o[8]));
  mux mux_10 (.a(a[9]), .b(b[9]), .sel(sel), .o(o[9]));
  mux mux_11 (.a(a[10]), .b(b[10]), .sel(sel), .o(o[10]));
  mux mux_12 (.a(a[11]), .b(b[11]), .sel(sel), .o(o[11]));
  mux mux_13 (.a(a[12]), .b(b[12]), .sel(sel), .o(o[12]));
  mux mux_14 (.a(a[13]), .b(b[13]), .sel(sel), .o(o[13]));
  mux mux_15 (.a(a[14]), .b(b[14]), .sel(sel), .o(o[14]));
  mux mux_16 (.a(a[15]), .b(b[15]), .sel(sel), .o(o[15]));
endmodule

module Mux4way16bit (
  input  [15:0] a,
  input  [15:0] b,
  input  [15:0] c,
  input  [15:0] d,
  input  [1:0] sel,
  output [15:0] o
);

  wire [15:0] mux16_1_o, mux16_2_o;

  mux16 mux16_1 (.sel(sel[0]), .a(a), .b(b), .o(mux16_1_o));
  mux16 mux16_2 (.sel(sel[0]), .a(c), .b(d), .o(mux16_2_o));
  mux16 mux16_3 (.sel(sel[1]), .a(mux16_1_o), .b(mux16_2_o), .o(o));
endmodule

module Mux8way16bit (
  input  [15:0] a,
  input  [15:0] b,
  input  [15:0] c,
  input  [15:0] d,
  input  [15:0] e,
  input  [15:0] f,
  input  [15:0] g,
  input  [15:0] h,
  input  [2:0] in_9,
  output [15:0] o
);

  wire [15:0] mux4way16bit_1_o, mux4way16bit_2_o;

  Mux4way16bit mux4way16bit_1 (.a(a), .b(b), .c(c), .d(d), .sel(in_9[1:0]), .o(mux4way16bit_1_o));
  Mux4way16bit mux4way16bit_2 (.a(e), .b(f), .c(g), .d(h), .sel(in_9[1:0]), .o(mux4way16bit_2_o));
  mux16 mux16_1 (.sel(in_9[2]), .a(mux4way16bit_1_o), .b(mux4way16bit_2_o), .o(o));
endmodule

module Dmux4way (
  input  x,
  input  [1:0] sel,
  output out_3,
  output out_4,
  output out_5,
  output out_6
);

  wire dmux_1_a, dmux_1_b;

  Dmux dmux_1 (.x(x), .sel(sel[1]), .a(dmux_1_a), .b(dmux_1_b));
  Dmux dmux_2 (.x(dmux_1_a), .sel(sel[0]), .a(out_3), .b(out_4));
  Dmux dmux_3 (.x(dmux_1_b), .sel(sel[0]), .a(out_5), .b(out_6));
endmodule

module Dmux8way (
  input  x,
  input  [2:0] sel,
  output a,
  output b,
  output c,
  output d,
  output e,
  output f,
  output g,
  output h
);

  wire dmux_1_a, dmux_1_b;

  Dmux dmux_1 (.x(x), .sel(sel[2]), .a(dmux_1_a), .b(dmux_1_b));
  Dmux4way dmux4way_1 (.x(dmux_1_a), .sel(sel[1:0]), .out_3(a), .out_4(b), .out_5(c), .out_6(d));
  Dmux4way dmux4way_2 (.x(dmux_1_b), .sel(sel[1:0]), .out_3(e), .out_4(f), .out_5(g), .out_6(h));
endmodule
