// Logisim project project3.circ as structural Verilog: 31 circuits, main circuit main
module main (
  input  in_1,
  input  [15:0] in_2,
  input  [3:0] in_3,
  input  [3:0] in_4,
  output [15:0] out_5
);

  Ram16by16 ram16by16_1 (.Load(in_1), .x(in_2), .writeaddress(in_3), .readAddress(in_4), .outp(out_5));
endmodule

module nandgate (
  input  b,
  input  a,
  output out_3
);

  wire pull_resistor_1_node, transistor_2_out;

  Pull_Resistor pull_resistor_1 (.node(pull_resistor_1_node));
  Pull_Resistor pull_resistor_2 (.node(a));
  Transistor transistor_1 (.in(pull_resistor_1_node), .out(out_3), .gate(a));
  Pull_Resistor pull_resistor_3 (.node(b));
  Pull_Resistor pull_resistor_4 (.node(out_3));
  Transistor transistor_2 (.in(out_3), .out(transistor_2_out), .gate(b));
  // also tied to GND on the sheet: transistor_2_out
  // also tied to VCC on the sheet: pull_resistor_1_node
endmodule

module notgate (
  input  in_1,
  output out_2
);

  nand nand_1 (out_2, in_1, in_1);
endmodule

module andgate (
  input  a,
  input  b,
  output o
);

  wire nand_1_out;

  nand nand_1 (nand_1_out, a, b);
  // Probe on nand_1_out
  notgate notgate_1 (.in_1(nand_1_out), .out_2(o));
endmodule

module orgate (
  input  a,
  input  b,
  output o
);

  wire notgate_1_out_2, notgate_2_out_2;

  notgate notgate_1 (.in_1(a), .out_2(notgate_1_out_2));
  notgate notgate_2 (.in_1(b), .out_2(notgate_2_out_2));
  nand nand_1 (o, notgate_1_out_2, notgate_2_out_2);
endmodule

module not16 (
  input  [15:0] x,
  output [15:0] o
);

  notgate notgate_1 (.in_1(x[0]), .out_2(o[0]));
  notgate notgate_2 (.in_1(x[1]), .out_2(o[1]));
  notgate notgate_3 (.in_1(x[2]), .out_2(o[2]));
  notgate notgate_4 (.in_1(x[3]), .out_2(o[3]));
  notgate notgate_5 (.in_1(x[4]), .out_2(o[4]));
  notgate notgate_6 (.in_1(x[5]), .out_2(o[5]));
  notgate notgate_7 (.in_1(x[6]), .out_2(o[6]));
  notgate notgate_8 (.in_1(x[7]), .out_2(o[7]));
  notgate notgate_9 (.in_1(x[8]), .out_2(o[8]));
  notgate notgate_10 (.in_1(x[9]), .out_2(o[9]));
  notgate notgate_11 (.in_1(x[10]), .out_2(o[10]));
  notgate notgate_12 (.in_1(x[11]), .out_2(o[11]));
  notgate notgate_13 (.in_1(x[12]), .out_2(o[12]));
  notgate notgate_14 (.in_1(x[13]), .out_2(o[13]));
  notgate notgate_15 (.in_1(x[14]), .out_2(o[14]));
  notgate notgate_16 (.in_1(x[15]), .out_2(o[15]));
endmodule

module and16 (
  input  [15:0] a,
  input  [15:0] b,
  output [15:0] o
);

  andgate andgate_1 (.a(a[0]), .b(b[0]), .o(o[0]));
  andgate andgate_2 (.a(a[1]), .b(b[1]), .o(o[1]));
  andgate andgate_3 (.a(a[2]), .b(b[2]), .o(o[2]));
  andgate andgate_4 (.a(a[3]), .b(b[3]), .o(o[3]));
  andgate andgate_5 (.a(a[4]), .b(b[4]), .o(o[4]));
  andgate andgate_6 (.a(a[5]), .b(b[5]), .o(o[5]));
  andgate andgate_7 (.a(a[6]), .b(b[6]), .o(o[6]));
  andgate andgate_8 (.a(a[7]), .b(b[7]), .o(o[7]));
  andgate andgate_9 (.a(a[8]), .b(b[8]), .o(o[8]));
  andgate andgate_10 (.a(a[9]), .b(b[9]), .o(o[9]));
  andgate andgate_11 (.a(a[10]), .b(b[10]), .o(o[10]));
  andgate andgate_12 (.a(a[11]), .b(b[11]), .o(o[11]));
  andgate andgate_13 (.a(a[12]), .b(b[12]), .o(o[12]));
  andgate andgate_14 (.a(a[13]), .b(b[13]), .o(o[13]));
  andgate andgate_15 (.a(a[14]), .b(b[14]), .o(o[14]));
  andgate andgate_16 (.a(a[15]), .b(b[15]), .o(o[15]));
endmodule

module or16 (
  input  [15:0] a,
  input  [15:0] b,
  output [15:0] o
);

  wire [15:0] and16_1_o, not16_1_o, not16_2_o;

  not16 not16_1 (.x(a), .o(not16_1_o));
  not16 not16_2 (.x(b), .o(not16_2_o));
  // Probe on not16_1_o
  // Probe on not16_2_o
  and16 and16_1 (.a(not16_1_o), .b(not16_2_o), .o(and16_1_o));
  // Probe on and16_1_o
  not16 not16_3 (.x(and16_1_o), .o(o));
endmodule

module xorgate (
  input  a,
  input  b,
  output o
);

  wire andgate_1_o, andgate_2_o, notgate_1_out_2, notgate_2_out_2;

  notgate notgate_1 (.in_1(a), .out_2(notgate_1_out_2));
  notgate notgate_2 (.in_1(b), .out_2(notgate_2_out_2));
  andgate andgate_1 (.a(a), .b(notgate_2_out_2), .o(andgate_1_o));
  andgate andgate_2 (.a(notgate_1_out_2), .b(b), .o(andgate_2_o));
  orgate orgate_1 (.a(andgate_1_o), .b(andgate_2_o), .o(o));
endmodule

module or8way (
  input  [7:0] a,
  output o
);

  wire orgate_1_o, orgate_2_o, orgate_3_o, orgate_4_o, orgate_5_o, orgate_6_o;

  orgate orgate_1 (.a(a[0]), .b(a[1]), .o(orgate_1_o));
  orgate orgate_2 (.a(orgate_1_o), .b(a[2]), .o(orgate_2_o));
  orgate orgate_3 (.a(orgate_2_o), .b(a[3]), .o(orgate_3_o));
  orgate orgate_4 (.a(a[4]), .b(a[5]), .o(orgate_4_o));
  orgate orgate_5 (.a(a[6]), .b(a[7]), .o(orgate_5_o));
  orgate orgate_6 (.a(orgate_3_o), .b(orgate_4_o), .o(orgate_6_o));
  orgate orgate_7 (.a(orgate_5_o), .b(orgate_6_o), .o(o));
endmodule

module mux (
  input  a,
  input  b,
  input  sel,
  output o
);

  wire andgate_1_o, andgate_2_o, notgate_1_out_2, orgate_1_o;

  orgate orgate_1 (.a(b), .b(notgate_1_out_2), .o(orgate_1_o));
  andgate andgate_1 (.a(orgate_1_o), .b(a), .o(andgate_1_o));
  notgate notgate_1 (.in_1(sel), .out_2(notgate_1_out_2));
  andgate andgate_2 (.a(b), .b(sel), .o(andgate_2_o));
  orgate orgate_2 (.a(andgate_2_o), .b(andgate_1_o), .o(o));
endmodule

module Dmux (
  input  x,
  input  sel,
  output a,
  output b
);

  wire notgate_1_out_2;

  notgate notgate_1 (.in_1(sel), .out_2(notgate_1_out_2));
  andgate andgate_1 (.a(x), .b(notgate_1_out_2), .o(a));
  andgate andgate_2 (.a(x), .b(sel), .o(b));
endmodule

module mux16 (
  input  sel,
  input  [15:0] a,
  input  [15:0] b,
  output [15:0] o
);

  mux mux_1 (.a(a[0]), .b(b[0]), .sel(sel), .o(o[0]));
  mux mux_2 (.a(a[1]), .b(b[1]), .sel(sel), .o(o[1]));
  mux mux_3 (.a(a[2]), .b(b[2]), .sel(sel), .o(o[2]));
  mux mux_4 (.a(a[3]), .b(b[3]), .sel(sel), .o(o[3]));
  mux mux_5 (.a(a[4]), .b(b[4]), .sel(sel), .o(o[4]));
  mux mux_6 (.a(a[5]), .b(b[5]), .sel(sel), .o(o[5]));
  mux mux_7 (.a(a[6]), .b(b[6]), .sel(sel), .o(o[6]));
  mux mux_8 (.a(a[7]), .b(b[7]), .sel(sel), .o(o[7]));
  mux mux_9 (.a(a[8]), .b(b[8]), .sel(sel), .o(o[8]));
  mux mux_10 (.a(a[9]), .b(b[9]), .sel(sel), .o(o[9]));
  mux mux_11 (.a(a[10]), .b(b[10]), .sel(sel), .o(o[10]));
  mux mux_12 (.a(a[11]), .b(b[11]), .sel(sel), .o(o[11]));
  mux mux_13 (.a(a[12]), .b(b[12]), .sel(sel), .o(o[12]));
  mux mux_14 (.a(a[13]), .b(b[13]), .sel(sel), .o(o[13]));
  mux mux_15 (.a(a[14]), .b(b[14]), .sel(sel), .o(o[14]));
  mux mux_16 (.a(a[15]), .b(b[15]), .sel(sel), .o(o[15]));
endmodule

module Mux4way16bit (
  input  [15:0] a,
  input  [15:0] b,
  input  [15:0] c,
  input  [15:0] d,
  input  [1:0] sel,
  output [15:0] o
);

  wire [15:0] mux16_1_o, mux16_2_o;

  mux16 mux16_1 (.sel(sel[0]), .a(a), .b(b), .o(mux16_1_o));
  mux16 mux16_2 (.sel(sel[0]), .a(c), .b(d), .o(mux16_2_o));
  mux16 mux16_3 (.sel(sel[1]), .a(mux16_1_o), .b(mux16_2_o), .o(o));
endmodule

module Mux8way16bit (
  input  [15:0] a,
  input  [15:0] b,
  input  [15:0] c,
  input  [15:0] d,
  input  [15:0] e,
  input  [15:0] f,
  input  [15:0] g,
  input  [15:0] h,
  input  [2:0] in_9,
  output [15:0] o
);

  wire [15:0] mux4way16bit_1_o, mux4way16bit_2_o;

  Mux4way16bit mux4way16bit_1 (.a(a), .b(b), .c(c), .d(d), .sel(in_9[1:0]), .o(mux4way16bit_1_o));
  Mux4way16bit mux4way16bit_2 (.a(e), .b(f), .c(g), .d(h), .sel(in_9[1:0]), .o(mux4way16bit_2_o));
  mux16 mux16_1 (.sel(in_9[2]), .a(mux4way16bit_1_o), .b(mux4way16bit_2_o), .o(o));
endmodule

module Dmux4way (
  input  x,
  input  [1:0] sel,
  output out_3,
  output out_4,
  output out_5,
  output out_6
);

  wire dmux_1_a, dmux_1_b;

  Dmux dmux_1 (.x(x), .sel(sel[1]), .a(dmux_1_a), .b(dmux_1_b));
  Dmux dmux_2 (.x(dmux_1_a), .sel(sel[0]), .a(out_3), .b(out_4));
  Dmux dmux_3 (.x(dmux_1_b), .sel(sel[0]), .a(out_5), .b(out_6));
endmodule

module Dmux8Way (
  input  x,
  input  [2:0] sel,
  output a,
  output b,
  output c,
  output d,
  output e,
  output f,
  output g,
  output h
);

  wire dmux_1_a, dmux_1_b;

  Dmux dmux_1 (.x(x), .sel(sel[2]), .a(dmux_1_a), .b(dmux_1_b));
  Dmux4way dmux4way_1 (.x(dmux_1_a), .sel(sel[1:0]), .out_3(a), .out_4(b), .out_5(c), .out_6(d));
  Dmux4way dmux4way_2 (.x(dmux_1_b), .sel(sel[1:0]), .out_3(e), .out_4(f), .out_5(g), .out_6(h));
endmodule

module HalfAdder (
  input  a,
  input  b,
  output sum,
  output carry
);

  xorgate xorgate_1 (.a(a), .b(b), .o(sum));
  andgate andgate_1 (.a(a), .b(b), .o(carry));
endmodule

module FullAdder (
  input  a,
  input  b,
  input  cin,
  output sum,
  output cout
);

  wire andgate_1_o, andgate_2_o, xorgate_1_o;

  andgate andgate_1 (.a(a), .b(b), .o(andgate_1_o));
  xorgate xorgate_1 (.a(a), .b(b), .o(xorgate_1_o));
  andgate andgate_2 (.a(xorgate_1_o), .b(cin), .o(andgate_2_o));
  xorgate xorgate_2 (.a(xorgate_1_o), .b(cin), .o(sum));
  orgate orgate_1 (.a(andgate_2_o), .b(andgate_1_o), .o(cout));
endmodule

module Add16bits (
  input  [15:0] a,
  input  [15:0] b,
  output [15:0] sum
);

  wire fulladder_1_cout, fulladder_2_cout, fulladder_3_cout, fulladder_4_cout, fulladder_5_cout,
       fulladder_6_cout, fulladder_7_cout, fulladder_8_cout, fulladder_9_cout, fulladder_10_cout,
       fulladder_11_cout, fulladder_12_cout, fulladder_13_cout, fulladder_14_cout, fulladder_15_cout,
       halfadder_1_carry;

  HalfAdder halfadder_1 (.a(a[0]), .b(b[0]), .sum(sum[0]), .carry(halfadder_1_carry));
  FullAdder fulladder_1 (.a(a[1]), .b(b[1]), .cin(halfadder_1_carry), .sum(sum[1]), .cout(fulladder_1_cout));
  FullAdder fulladder_2 (.a(a[2]), .b(b[2]), .cin(fulladder_1_cout), .sum(sum[2]), .cout(fulladder_2_cout));
  FullAdder fulladder_3 (.a(a[3]), .b(b[3]), .cin(fulladder_2_cout), .sum(sum[3]), .cout(fulladder_3_cout));
  FullAdder fulladder_4 (.a(a[4]), .b(b[4]), .cin(fulladder_3_cout), .sum(sum[4]), .cout(fulladder_4_cout));
  FullAdder fulladder_5 (.a(a[5]), .b(b[5]), .cin(fulladder_4_cout), .sum(sum[5]), .cout(fulladder_5_cout));
  FullAdder fulladder_6 (.a(a[6]), .b(b[6]), .cin(fulladder_5_cout), .sum(sum[6]), .cout(fulladder_6_cout));
  FullAdder fulladder_7 (.a(a[7]), .b(b[7]), .cin(fulladder_6_cout), .sum(sum[7]), .cout(fulladder_7_cout));
  FullAdder fulladder_8 (.a(a[8]), .b(b[8]), .cin(fulladder_7_cout), .sum(sum[8]), .cout(fulladder_8_cout));
  FullAdder fulladder_9 (.a(a[9]), .b(b[9]), .cin(fulladder_8_cout), .sum(sum[9]), .cout(fulladder_9_cout));
  FullAdder fulladder_10 (.a(a[10]), .b(b[10]), .cin(fulladder_9_cout), .sum(sum[10]), .cout(fulladder_10_cout));
  FullAdder fulladder_11 (.a(a[11]), .b(b[11]), .cin(fulladder_10_cout), .sum(sum[11]), .cout(fulladder_11_cout));
  FullAdder fulladder_12 (.a(a[12]), .b(b[12]), .cin(fulladder_11_cout), .sum(sum[12]), .cout(fulladder_12_cout));
  FullAdder fulladder_13 (.a(a[13]), .b(b[13]), .cin(fulladder_12_cout), .sum(sum[13]), .cout(fulladder_13_cout));
  FullAdder fulladder_14 (.a(a[14]), .b(b[14]), .cin(fulladder_13_cout), .sum(sum[14]), .cout(fulladder_14_cout));
  FullAdder fulladder_15 (.a(a[15]), .b(b[15]), .cin(fulladder_14_cout), .sum(sum[15]), .cout(fulladder_15_cout));
  // Probe on fulladder_15_cout
endmodule

module Inc16 (
  input  [15:0] x,
  output [15:0] result
);

  Add16bits add16bits_1 (.a(x), .b(16'h1), .sum(result));
endmodule

module ALU (
  input  nx,
  input  zx,
  input  f,
  input  no,
  input  [15:0] x,
  input  ny,
  input  zy,
  input  [15:0] y,
  output [15:0] OUTP,
  output zr,
  output nr
);

  wire or8way_1_o, or8way_2_o, orgate_1_o;
  wire [15:0] add16bits_1_sum, and16_1_o, and16_2_o, and16_3_o, mux16_1_o, mux16_2_o, mux16_3_o, mux16_4_o,
       mux16_5_o, not16_1_o, not16_2_o, not16_3_o;

  and16 and16_1 (.a(x), .b({16{1'b0}}), .o(and16_1_o));
  and16 and16_2 (.a(y), .b({16{1'b0}}), .o(and16_2_o));
  // Probe on mux16_1_o
  mux16 mux16_1 (.sel(zx), .a(x), .b(and16_1_o), .o(mux16_1_o));
  // Probe on mux16_2_o
  mux16 mux16_2 (.sel(zy), .a(y), .b(and16_2_o), .o(mux16_2_o));
  not16 not16_1 (.x(mux16_1_o), .o(not16_1_o));
  not16 not16_2 (.x(mux16_2_o), .o(not16_2_o));
  // Probe on mux16_3_o
  mux16 mux16_3 (.sel(nx), .a(mux16_1_o), .b(not16_1_o), .o(mux16_3_o));
  // Probe on mux16_4_o
  mux16 mux16_4 (.sel(ny), .a(mux16_2_o), .b(not16_2_o), .o(mux16_4_o));
  // Probe on mux16_5_o
  Add16bits add16bits_1 (.a(mux16_3_o), .b(mux16_4_o), .sum(add16bits_1_sum));
  and16 and16_3 (.a(mux16_3_o), .b(mux16_4_o), .o(and16_3_o));
  mux16 mux16_5 (.sel(f), .a(and16_3_o), .b(add16bits_1_sum), .o(mux16_5_o));
  or8way or8way_1 (.a(OUTP[7:0]), .o(or8way_1_o));
  or8way or8way_2 (.a({nr, OUTP[14:8]}), .o(or8way_2_o));
  not16 not16_3 (.x(mux16_5_o), .o(not16_3_o));
  orgate orgate_1 (.a(or8way_1_o), .b(or8way_2_o), .o(orgate_1_o));
  mux16 mux16_6 (.sel(no), .a(mux16_5_o), .b(not16_3_o), .o({nr, OUTP[14:0]}));
  notgate notgate_1 (.in_1(orgate_1_o), .out_2(zr));

  assign OUTP[15] = nr;
endmodule

module onebitforever (
  input  in_1,
  input  in_2,
  output out_3
);

  wire clock_1_out, mux_1_o;

  mux mux_1 (.a(out_3), .b(in_1), .sel(in_2), .o(mux_1_o));
  Clock clock_1 (.out(clock_1_out));
  D_Flip_Flop d_ff_1 (.D(mux_1_o), .clk(clock_1_out), .Q(out_3));  // open: Qn, preset, reset
endmodule

module register16bits (
  input  load,
  input  [15:0] \int ,
  output [15:0] outp
);

  onebitforever onebitforever_1 (.in_1(\int [0]), .in_2(load), .out_3(outp[0]));
  onebitforever onebitforever_2 (.in_1(\int [1]), .in_2(load), .out_3(outp[1]));
  onebitforever onebitforever_3 (.in_1(\int [2]), .in_2(load), .out_3(outp[2]));
  onebitforever onebitforever_4 (.in_1(\int [3]), .in_2(load), .out_3(outp[3]));
  onebitforever onebitforever_5 (.in_1(\int [4]), .in_2(load), .out_3(outp[4]));
  onebitforever onebitforever_6 (.in_1(\int [5]), .in_2(load), .out_3(outp[5]));
  onebitforever onebitforever_7 (.in_1(\int [6]), .in_2(load), .out_3(outp[6]));
  onebitforever onebitforever_8 (.in_1(\int [7]), .in_2(load), .out_3(outp[7]));
  onebitforever onebitforever_9 (.in_1(\int [8]), .in_2(load), .out_3(outp[8]));
  onebitforever onebitforever_10 (.in_1(\int [9]), .in_2(load), .out_3(outp[9]));
  onebitforever onebitforever_11 (.in_1(\int [10]), .in_2(load), .out_3(outp[10]));
  onebitforever onebitforever_12 (.in_1(\int [11]), .in_2(load), .out_3(outp[11]));
  onebitforever onebitforever_13 (.in_1(\int [12]), .in_2(load), .out_3(outp[12]));
  onebitforever onebitforever_14 (.in_1(\int [13]), .in_2(load), .out_3(outp[13]));
  onebitforever onebitforever_15 (.in_1(\int [14]), .in_2(load), .out_3(outp[14]));
  onebitforever onebitforever_16 (.in_1(\int [15]), .in_2(load), .out_3(outp[15]));
endmodule

module Ram16by16 (
  input  Load,
  input  [15:0] x,
  input  [3:0] writeaddress,
  input  [3:0] readAddress,
  output [15:0] outp
);

  wire [15:0] dmux16way16bits_1_a, dmux16way16bits_1_b, dmux16way16bits_1_c, dmux16way16bits_1_d,
       dmux16way16bits_1_e, dmux16way16bits_1_f, dmux16way16bits_1_g, dmux16way16bits_1_h,
       dmux16way16bits_1_i, dmux16way16bits_1_j, dmux16way16bits_1_k, dmux16way16bits_1_l,
       dmux16way16bits_1_m, dmux16way16bits_1_n, dmux16way16bits_1_o, dmux16way16bits_1_p,
       register16bits_1_outp, register16bits_2_outp, register16bits_3_outp, register16bits_4_outp,
       register16bits_5_outp, register16bits_6_outp, register16bits_7_outp, register16bits_8_outp,
       register16bits_9_outp, register16bits_10_outp, register16bits_11_outp, register16bits_12_outp,
       register16bits_13_outp, register16bits_14_outp, register16bits_15_outp, register16bits_16_outp;

  Dmux16way16bits dmux16way16bits_1 (
    .x(x), .sel(writeaddress), .a(dmux16way16bits_1_a), .b(dmux16way16bits_1_b), .c(dmux16way16bits_1_c),
    .d(dmux16way16bits_1_d), .e(dmux16way16bits_1_e), .f(dmux16way16bits_1_f), .g(dmux16way16bits_1_g),
    .h(dmux16way16bits_1_h), .i(dmux16way16bits_1_i), .j(dmux16way16bits_1_j), .k(dmux16way16bits_1_k),
    .l(dmux16way16bits_1_l), .m(dmux16way16bits_1_m), .n(dmux16way16bits_1_n), .o(dmux16way16bits_1_o),
    .p(dmux16way16bits_1_p));
  register16bits register16bits_1 (.load(Load), .\int (dmux16way16bits_1_a), .outp(register16bits_1_outp));
  register16bits register16bits_2 (.load(Load), .\int (dmux16way16bits_1_b), .outp(register16bits_2_outp));
  register16bits register16bits_3 (.load(Load), .\int (dmux16way16bits_1_c), .outp(register16bits_3_outp));
  register16bits register16bits_4 (.load(Load), .\int (dmux16way16bits_1_d), .outp(register16bits_4_outp));
  register16bits register16bits_5 (.load(Load), .\int (dmux16way16bits_1_e), .outp(register16bits_5_outp));
  register16bits register16bits_6 (.load(Load), .\int (dmux16way16bits_1_f), .outp(register16bits_6_outp));
  register16bits register16bits_7 (.load(Load), .\int (dmux16way16bits_1_g), .outp(register16bits_7_outp));
  register16bits register16bits_8 (.load(Load), .\int (dmux16way16bits_1_h), .outp(register16bits_8_outp));
  register16bits register16bits_9 (.load(Load), .\int (dmux16way16bits_1_i), .outp(register16bits_9_outp));
  register16bits register16bits_10 (.load(Load), .\int (dmux16way16bits_1_j), .outp(register16bits_10_outp));
  register16bits register16bits_11 (.load(Load), .\int (dmux16way16bits_1_k), .outp(register16bits_11_outp));
  register16bits register16bits_12 (.load(Load), .\int (dmux16way16bits_1_l), .outp(register16bits_12_outp));
  register16bits register16bits_13 (.load(Load), .\int (dmux16way16bits_1_m), .outp(register16bits_13_outp));
  register16bits register16bits_14 (.load(Load), .\int (dmux16way16bits_1_n), .outp(register16bits_14_outp));
  register16bits register16bits_15 (.load(Load), .\int (dmux16way16bits_1_o), .outp(register16bits_15_outp));
  register16bits register16bits_16 (.load(Load), .\int (dmux16way16bits_1_p), .outp(register16bits_16_outp));
  Mux16way16bit mux16way16bit_1 (
    .a(register16bits_1_outp), .b(register16bits_2_outp), .c(register16bits_3_outp),
    .d(register16bits_4_outp), .e(register16bits_5_outp), .f(register16bits_6_outp),
    .g(register16bits_7_outp), .h(register16bits_8_outp), .i(register16bits_9_outp), .sel(readAddress),
    .j(register16bits_10_outp), .k(register16bits_11_outp), .l(register16bits_12_outp),
    .m(register16bits_13_outp), .n(register16bits_14_outp), .o(register16bits_15_outp),
    .p(register16bits_16_outp), .outp(outp));
endmodule

module Mux16way16bit (
  input  [15:0] a,
  input  [15:0] b,
  input  [15:0] c,
  input  [15:0] d,
  input  [15:0] e,
  input  [15:0] f,
  input  [15:0] g,
  input  [15:0] h,
  input  [15:0] i,
  input  [3:0] sel,
  input  [15:0] j,
  input  [15:0] k,
  input  [15:0] l,
  input  [15:0] m,
  input  [15:0] n,
  input  [15:0] o,
  input  [15:0] p,
  output [15:0] outp
);

  wire [15:0] mux8way16bit_1_o, mux8way16bit_2_o;

  Mux8way16bit mux8way16bit_1 (
    .a(a), .b(b), .c(c), .d(d), .e(e), .f(f), .g(g), .h(h), .in_9(sel[2:0]), .o(mux8way16bit_1_o));
  Mux8way16bit mux8way16bit_2 (
    .a(i), .b(j), .c(k), .d(l), .e(m), .f(n), .g(o), .h(p), .in_9(sel[2:0]), .o(mux8way16bit_2_o));
  mux16 mux16_1 (.sel(sel[3]), .a(mux8way16bit_1_o), .b(mux8way16bit_2_o), .o(outp));
endmodule

module Dmux8way16bits (
  input  [15:0] x,
  input  [2:0] sel,
  output [15:0] a,
  output [15:0] b,
  output [15:0] c,
  output [15:0] d,
  output [15:0] e,
  output [15:0] f,
  output [15:0] g,
  output [15:0] h
);

  wire [15:0] dmux16_1_a, dmux16_1_b;

  Dmux16 dmux16_1 (.sel(sel[2]), .x(x), .a(dmux16_1_a), .b(dmux16_1_b));
  Dmux4way16bits dmux4way16bits_1 (.in_1(dmux16_1_a), .in_2(sel[1:0]), .a(a), .b(b), .c(c), .d(d));
  Dmux4way16bits dmux4way16bits_2 (.in_1(dmux16_1_b), .in_2(sel[1:0]), .a(e), .b(f), .c(g), .d(h));
endmodule

module Dmux16 (
  input  sel,
  input  [15:0] x,
  output [15:0] a,
  output [15:0] b
);

  Dmux dmux_1 (.x(x[0]), .sel(sel), .a(a[0]), .b(b[0]));
  Dmux dmux_2 (.x(x[1]), .sel(sel), .a(a[1]), .b(b[1]));
  Dmux dmux_3 (.x(x[2]), .sel(sel), .a(a[2]), .b(b[2]));
  Dmux dmux_4 (.x(x[3]), .sel(sel), .a(a[3]), .b(b[3]));
  Dmux dmux_5 (.x(x[4]), .sel(sel), .a(a[4]), .b(b[4]));
  Dmux dmux_6 (.x(x[5]), .sel(sel), .a(a[5]), .b(b[5]));
  Dmux dmux_7 (.x(x[6]), .sel(sel), .a(a[6]), .b(b[6]));
  Dmux dmux_8 (.x(x[7]), .sel(sel), .a(a[7]), .b(b[7]));
  Dmux dmux_9 (.x(x[8]), .sel(sel), .a(a[8]), .b(b[8]));
  Dmux dmux_10 (.x(x[9]), .sel(sel), .a(a[9]), .b(b[9]));
  Dmux dmux_11 (.x(x[10]), .sel(sel), .a(a[10]), .b(b[10]));
  Dmux dmux_12 (.x(x[11]), .sel(sel), .a(a[11]), .b(b[11]));
  Dmux dmux_13 (.x(x[12]), .sel(sel), .a(a[12]), .b(b[12]));
  Dmux dmux_14 (.x(x[13]), .sel(sel), .a(a[13]), .b(b[13]));
  Dmux dmux_15 (.x(x[14]), .sel(sel), .a(a[14]), .b(b[14]));
  Dmux dmux_16 (.x(x[15]), .sel(sel), .a(a[15]), .b(b[15]));
endmodule

module Dmux4way16bits (
  input  [15:0] in_1,
  input  [1:0] in_2,
  output [15:0] a,
  output [15:0] b,
  output [15:0] c,
  output [15:0] d
);

  wire [15:0] dmux16_1_a, dmux16_1_b;

  Dmux16 dmux16_1 (.sel(in_2[1]), .x(in_1), .a(dmux16_1_a), .b(dmux16_1_b));
  Dmux16 dmux16_2 (.sel(in_2[0]), .x(dmux16_1_a), .a(a), .b(b));
  Dmux16 dmux16_3 (.sel(in_2[0]), .x(dmux16_1_b), .a(c), .b(d));
endmodule

module Dmux16way16bits (
  input  [15:0] x,
  input  [3:0] sel,
  output [15:0] a,
  output [15:0] b,
  output [15:0] c,
  output [15:0] d,
  output [15:0] e,
  output [15:0] f,
  output [15:0] g,
  output [15:0] h,
  output [15:0] i,
  output [15:0] j,
  output [15:0] k,
  output [15:0] l,
  output [15:0] m,
  output [15:0] n,
  output [15:0] o,
  output [15:0] p
);

  wire [15:0] dmux16_1_a, dmux16_1_b;

  Dmux16 dmux16_1 (.sel(sel[3]), .x(x), .a(dmux16_1_a), .b(dmux16_1_b));
  Dmux8way16bits dmux8way16bits_1 (
    .x(dmux16_1_a), .sel(sel[2:0]), .a(a), .b(b), .c(c), .d(d), .e(e), .f(f), .g(g), .h(h));
  Dmux8way16bits dmux8way16bits_2 (
    .x(dmux16_1_b), .sel(sel[2:0]), .a(i), .b(j), .c(k), .d(l), .e(m), .f(n), .g(o), .h(p));
endmodule

module Ram8bit (
  input  load,
  input  [15:0] inp,
  input  [2:0] address,
  output [15:0] outp
);

  Ram16by16 ram16by16_1 (
    .Load(load), .x(inp), .writeaddress({1'b0, address}), .readAddress({1'b0, address}), .outp(outp));
endmodule
