// Logisim project project3builtin.circ as structural Verilog
module Ram8bits (
  input  load,
  input  [15:0] inp,
  input  [2:0] address,
  output [15:0] outp
);

  wire clock_1_out;

  Clock clock_1 (.out(clock_1_out));
  RAM ram_1 (.addr({{5{1'b0}}, address}), .we(load), .oe(1'b1), .clk(clock_1_out), .din(inp[7:0]), .dout(outp[7:0]));
  RAM ram_2 (.addr({{5{1'b0}}, address}), .we(load), .oe(1'b1), .clk(clock_1_out), .din(inp[15:8]), .dout(outp[15:8]));
endmodule

module Ram64bits (
  input  load,
  input  [15:0] inp,
  input  [5:0] address,
  output [15:0] outp
);

  wire demultiplexer_1_out0, demultiplexer_1_out1, demultiplexer_1_out2, demultiplexer_1_out3,
       demultiplexer_1_out4, demultiplexer_1_out5, demultiplexer_1_out6, demultiplexer_1_out7;
  wire [15:0] ram8bits_1_outp, ram8bits_2_outp, ram8bits_3_outp, ram8bits_4_outp, ram8bits_5_outp,
       ram8bits_6_outp, ram8bits_7_outp, ram8bits_8_outp;

  Demultiplexer #(.select(3)) demultiplexer_1 (
    .out0(demultiplexer_1_out0), .out1(demultiplexer_1_out1), .out2(demultiplexer_1_out2),
    .out3(demultiplexer_1_out3), .out4(demultiplexer_1_out4), .out5(demultiplexer_1_out5),
    .out6(demultiplexer_1_out6), .out7(demultiplexer_1_out7), .in(load), .sel(address[5:3]));
  Ram8bits ram8bits_1 (.load(demultiplexer_1_out0), .inp(inp), .address(address[2:0]), .outp(ram8bits_1_outp));
  Ram8bits ram8bits_2 (.load(demultiplexer_1_out1), .inp(inp), .address(address[2:0]), .outp(ram8bits_2_outp));
  Ram8bits ram8bits_3 (.load(demultiplexer_1_out2), .inp(inp), .address(address[2:0]), .outp(ram8bits_3_outp));
  Ram8bits ram8bits_4 (.load(demultiplexer_1_out3), .inp(inp), .address(address[2:0]), .outp(ram8bits_4_outp));
  Ram8bits ram8bits_5 (.load(demultiplexer_1_out4), .inp(inp), .address(address[2:0]), .outp(ram8bits_5_outp));
  Ram8bits ram8bits_6 (.load(demultiplexer_1_out5), .inp(inp), .address(address[2:0]), .outp(ram8bits_6_outp));
  Ram8bits ram8bits_7 (.load(demultiplexer_1_out6), .inp(inp), .address(address[2:0]), .outp(ram8bits_7_outp));
  Ram8bits ram8bits_8 (.load(demultiplexer_1_out7), .inp(inp), .address(address[2:0]), .outp(ram8bits_8_outp));
  Multiplexer #(.select(3), .width(16)) multiplexer_1 (
    .in0(ram8bits_1_outp), .in1(ram8bits_2_outp), .in2(ram8bits_3_outp), .in3(ram8bits_4_outp),
    .in4(ram8bits_5_outp), .in5(ram8bits_6_outp), .in6(ram8bits_7_outp), .in7(ram8bits_8_outp), .out(outp),
    .sel(address[5:3]));
endmodule

module Ram512 (
  input  load,
  input  [15:0] inp,
  input  [8:0] address,
  output [15:0] outp
);

  wire demultiplexer_1_out0, demultiplexer_1_out1, demultiplexer_1_out2, demultiplexer_1_out3,
       demultiplexer_1_out4, demultiplexer_1_out5, demultiplexer_1_out6, demultiplexer_1_out7;
  wire [15:0] ram64bits_1_outp, ram64bits_2_outp, ram64bits_3_outp, ram64bits_4_outp, ram64bits_5_outp,
       ram64bits_6_outp, ram64bits_7_outp, ram64bits_8_outp;

  Demultiplexer #(.select(3)) demultiplexer_1 (
    .out0(demultiplexer_1_out0), .out1(demultiplexer_1_out1), .out2(demultiplexer_1_out2),
    .out3(demultiplexer_1_out3), .out4(demultiplexer_1_out4), .out5(demultiplexer_1_out5),
    .out6(demultiplexer_1_out6), .out7(demultiplexer_1_out7), .in(load), .sel(address[8:6]));
  Ram64bits ram64bits_1 (.load(demultiplexer_1_out0), .inp(inp), .address(address[5:0]), .outp(ram64bits_1_outp));
  Ram64bits ram64bits_2 (.load(demultiplexer_1_out1), .inp(inp), .address(address[5:0]), .outp(ram64bits_2_outp));
  Ram64bits ram64bits_3 (.load(demultiplexer_1_out2), .inp(inp), .address(address[5:0]), .outp(ram64bits_3_outp));
  Ram64bits ram64bits_4 (.load(demultiplexer_1_out3), .inp(inp), .address(address[5:0]), .outp(ram64bits_4_outp));
  Ram64bits ram64bits_5 (.load(demultiplexer_1_out4), .inp(inp), .address(address[5:0]), .outp(ram64bits_5_outp));
  Ram64bits ram64bits_6 (.load(demultiplexer_1_out5), .inp(inp), .address(address[5:0]), .outp(ram64bits_6_outp));
  Ram64bits ram64bits_7 (.load(demultiplexer_1_out6), .inp(inp), .address(address[5:0]), .outp(ram64bits_7_outp));
  Ram64bits ram64bits_8 (.load(demultiplexer_1_out7), .inp(inp), .address(address[5:0]), .outp(ram64bits_8_outp));
  Multiplexer #(.select(3), .width(16)) multiplexer_1 (
    .in0(ram64bits_1_outp), .in1(ram64bits_2_outp), .in2(ram64bits_3_outp), .in3(ram64bits_4_outp),
    .in4(ram64bits_5_outp), .in5(ram64bits_6_outp), .in6(ram64bits_7_outp), .in7(ram64bits_8_outp),
    .out(outp), .sel(address[8:6]));
endmodule

module Ram4k (
  input  load,
  input  [15:0] inp,
  input  [11:0] address,
  output [15:0] outp
);

  wire demultiplexer_1_out0, demultiplexer_1_out1, demultiplexer_1_out2, demultiplexer_1_out3,
       demultiplexer_1_out4, demultiplexer_1_out5, demultiplexer_1_out6, demultiplexer_1_out7;
  wire [15:0] ram512_1_outp, ram512_2_outp, ram512_3_outp, ram512_4_outp, ram512_5_outp, ram512_6_outp,
       ram512_8_outp, ram512_9_outp;

  Demultiplexer #(.select(3)) demultiplexer_1 (
    .out0(demultiplexer_1_out0), .out1(demultiplexer_1_out1), .out2(demultiplexer_1_out2),
    .out3(demultiplexer_1_out3), .out4(demultiplexer_1_out4), .out5(demultiplexer_1_out5),
    .out6(demultiplexer_1_out6), .out7(demultiplexer_1_out7), .in(load), .sel(address[11:9]));
  Ram512 ram512_1 (.load(demultiplexer_1_out0), .inp(inp), .address(address[8:0]), .outp(ram512_1_outp));
  Ram512 ram512_2 (.load(demultiplexer_1_out1), .inp(inp), .address(address[8:0]), .outp(ram512_2_outp));
  Ram512 ram512_3 (.load(demultiplexer_1_out2), .inp(inp), .address(address[8:0]), .outp(ram512_3_outp));
  Ram512 ram512_4 (.load(demultiplexer_1_out3), .inp(inp), .address(address[8:0]), .outp(ram512_4_outp));
  Ram512 ram512_5 (.load(demultiplexer_1_out4), .inp(inp), .address(address[8:0]), .outp(ram512_5_outp));
  Ram512 ram512_6 (.load(demultiplexer_1_out5), .inp(inp), .address(address[8:0]), .outp(ram512_6_outp));
  Ram512 ram512_7 (.load(demultiplexer_1_out5), .inp(inp), .address(address[8:0]), .outp(ram512_6_outp));
  Ram512 ram512_8 (.load(demultiplexer_1_out6), .inp(inp), .address(address[8:0]), .outp(ram512_8_outp));
  Ram512 ram512_9 (.load(demultiplexer_1_out7), .inp(inp), .address(address[8:0]), .outp(ram512_9_outp));
  Multiplexer #(.select(3), .width(16)) multiplexer_1 (
    .in0(ram512_1_outp), .in1(ram512_2_outp), .in2(ram512_3_outp), .in3(ram512_4_outp), .in4(ram512_5_outp),
    .in5(ram512_6_outp), .in6(ram512_8_outp), .in7(ram512_9_outp), .out(outp), .sel(address[11:9]));
endmodule

module Ram16k (
  input  load,
  input  [15:0] inp,
  input  [13:0] address,
  output [15:0] outp
);

  wire demultiplexer_1_out0, demultiplexer_1_out1, demultiplexer_1_out2, demultiplexer_1_out3;
  wire [15:0] ram4k_1_outp, ram4k_2_outp, ram4k_3_outp, ram4k_4_outp;

  Demultiplexer #(.select(2)) demultiplexer_1 (
    .out0(demultiplexer_1_out0), .out1(demultiplexer_1_out1), .out2(demultiplexer_1_out2),
    .out3(demultiplexer_1_out3), .in(load), .sel(address[13:12]));
  Ram4k ram4k_1 (.load(demultiplexer_1_out0), .inp(inp), .address(address[11:0]), .outp(ram4k_1_outp));
  Ram4k ram4k_2 (.load(demultiplexer_1_out1), .inp(inp), .address(address[11:0]), .outp(ram4k_2_outp));
  Ram4k ram4k_3 (.load(demultiplexer_1_out2), .inp(inp), .address(address[11:0]), .outp(ram4k_3_outp));
  Ram4k ram4k_4 (.load(demultiplexer_1_out3), .inp(inp), .address(address[11:0]), .outp(ram4k_4_outp));
  Multiplexer #(.select(2), .width(16)) multiplexer_1 (
    .in0(ram4k_1_outp), .in1(ram4k_2_outp), .in2(ram4k_3_outp), .in3(ram4k_4_outp), .out(outp),
    .sel(address[13:12]));
endmodule

module PC (
  input  [15:0] inp,
  input  load,
  input  inc,
  input  reset,
  output [15:0] out_5
);

  wire clock_1_out;
  wire [15:0] adder_1_out, multiplexer_1_out;

  Adder #(.width(16)) adder_1 (.a(out_5), .b(16'h1), .out(adder_1_out));  // open: cin, cout
  Multiplexer #(.select(3), .width(16)) multiplexer_1 (
    .in0(out_5), .in1({16{1'b0}}), .in2(adder_1_out), .in3({16{1'b0}}), .in4(inp), .in5({16{1'b0}}),
    .in6(inp), .in7({16{1'b0}}), .out(multiplexer_1_out), .sel({load, inc, reset}));
  Register #(.width(16)) register_1 (.D(multiplexer_1_out), .en(1'b1), .clk(clock_1_out), .Q(out_5));  // open: clr
  Clock clock_1 (.out(clock_1_out));
endmodule
